# Fritzing sketch OpenerPcr (saved by Fritzing 0.8.5b)
breadboards: 2

parts:
  Part1 = 2 Module relay
  J1 = Peltier Element
  +12VDC_rail = Power plug [part_number="ATX power supply +12VDC rail"]
  +5VDC_rail = Power plug [part_number="ATX power supply +5VDC rail"]
  Part2 = Arduino Uno (Rev3)
  FAN = Peltier Element

nets:
  VCC: Part1.VCC, Part1.JD-VCC, +5VDC_rail.VCC, Part2.5V
  N1: Part1.IN2, Part2.D3_PWM
  N2: Part1.IN1, Part2.D2
  GND: Part1.GND, +5VDC_rail.GND
  N3: Part1.NO2, Part1.NO1, +12VDC_rail.VCC, FAN.pin1
  N4: Part1.COM2, J1.pin2
  N5: Part1.NC2, Part1.NC1, +12VDC_rail.GND, FAN.pin2
  N6: Part1.COM1, J1.pin1

notes:
  Fan part not available in Fritzing. Use Peltier part instead.

custom parts:
  2 Module relay: This module can be used with Arduino Special Sensor Shield V4.0 You can do some simple design about it This is 2-Channel 5V Relay Module for Arduino PIC ARM AVR DSP It can be able to control various appliances, and other equipments with large current Easy to be controlled by a lots of Microcontrollers (Such as Arduino , 8051, AVR, PIC, DSP, ARM, ARM, MSP430, PLC,TTL logic) Just use 5v input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
